# Fritzing sketch ice gauge (saved by Fritzing 1.0.1rc)
breadboards: 1

parts:
  Mod1 = Raspberry Pi Pico
  J1 = Basic Servo
  Grove1 = Grove OLED 128x96
  J2 = Basic Servo
  S1 = Momentary Switch [package=ksa_sealed_tac_switch]

nets:
  N1: Mod1.pin_1, J1.pulse
  N2: Mod1.pin_2, J2.pulse
  GND: Mod1.pin_3, Mod1.pin_8, Mod1.pin_13, Mod1.pin_18, Mod1.pin_23, Mod1.pin_28, Mod1.pin_33, Mod1.pin_38, Mod1.pin_42, J1.gnd, Grove1.GND, J2.gnd, S1.4
  N3: Mod1.pin_6, Grove1.SDA
  N4: Mod1.pin_7, Grove1.SCL
  N5: Mod1.pin_10, S1.3
  N6: Mod1.pin_11, S1.2
  VCC: Mod1.pin_40, J1.vcc, Grove1.VCC, J2.vcc, S1.1

custom parts:
  Raspberry Pi Pico: Raspberry Pi Pico. Based around the RP2040 microcontroller the Pico is a low cost microcontroller device bringing Raspberry Pi quality, cost, and easy of use to the microcontroller space. Jan 2021, Split part in to two versions: tht (this one) and SMD. This one will drill holes for a .1 in header in pcb to allow plugging in the module as well as providing pads to solder the module to the top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
